# Fritzing sketch esp32_telegram_bot (saved by Fritzing 0.9.3b)

parts:
  A1 = ESP32 DevKitc V4
  KY-1 = Keyes Relay [package=THT]
  J2 = female pin header, 2 pins [form="♀ (female)"]
  S8 = Round Pushbutton

nets:
  N1: A1.Pin_14, A1.Pin_38, KY-1.ground, J2.pin1, S8.leg1
  N2: A1.Pin_19, KY-1.power, J2.pin2
  N3: A1.Pin_36, S8.leg0
  N4: A1.Pin_37, KY-1.signal

notes:
  5V Power supply
  INPUT_PULLUP

custom parts:
  ESP32 DevKitc V4: ESP32-DevKitC board with ESP32-WROOM-32 module. ESP32-DevKitC V4 is a small-sized ESP32-based development board produced by Espressif. Most of the pins on the ESP module are broken out to the pin headers on the board. The pins D0, D1, D2, D3, CMD and CLK are used internally for communication between ESP32 and SPI flash memory. They are grouped on both sides near the USB connector. Avoid using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
  Keyes Relay: The Keyes 5V relay module is suitable for SCM development, home appliance control. It uses a 5V~12V TIL control signal which can control DC / AC signal.
